# Fritzing sketch circuits (saved by Fritzing 0.8.3b)

parts:
  Part1 = Arduino Uno (Rev3)
  BeagleBone1 = BeagleBone Black
  J1 = ATX24 Pin Power Supply Connector [package=atx24_right_angle]
  Part2 = Logic Level Converter
  LPD8806_RGB_LED_Strip1 = LPD8806 RGB LED Strip
  JP1 = Header 2 [package=r_sw_th]

nets:
  N1: Part1.A4/SDA, Part2.TX_HV
  N2: Part1.A5/SCL, Part2.TX2_HV
  GND: Part1.GND, BeagleBone1.no_name_yet#34, BeagleBone1.no_name_yet#45, J1.GND, Part2.GND, JP1.1
  N3: Part1.5V, Part2.HV
  VIN: Part1.VIN, J1.12V
  N4: BeagleBone1.no_name_yet#19, Part2.TX_LV
  N5: BeagleBone1.no_name_yet#20, Part2.TX2_LV
  N6: BeagleBone1.no_name_yet#28, LPD8806_RGB_LED_Strip1.CI
  N7: BeagleBone1.no_name_yet#29, LPD8806_RGB_LED_Strip1.DI
  N8: BeagleBone1.no_name_yet#32, Part2.LV
  N9: BeagleBone1.no_name_yet#46, LPD8806_RGB_LED_Strip1.GND
  5V: J1.5V, LPD8806_RGB_LED_Strip1.+5V
  N10: J1.PS_ON, JP1.2

custom parts:
  BeagleBone Black: BeagleBone Black rev. A5B
  LPD8806 RGB LED Strip: Digitally addressable RGB LED strip
